// Digital circuit pruebadiseno.dig as structural Verilog
module pruebadiseno (
  input  y,
  input  x,
  input  s,
  output out_4
);

  wire _7402_1_pin1, _7402_1_pin2, _7402_1_pin3, _7402_1_pin4, _7402_1_pin5, _7402_1_pin6, _7402_1_pin7,
       _7408_1_pin6, _7408_1_pin8, _7408_1_pin9, _7408_1_pin10, _7408_1_pin11, o, s_t, x_t, y_t;

  // Not not_1 is placed but not wired
  _7408 _7408_1 (
    .pin1(x_t), .pin2(x_t), .pin3(o), .pin4(y_t), .pin5(y_t), .pin6(_7408_1_pin6), .pin7(1'b0),
    .pin8(_7408_1_pin8), .pin9(_7408_1_pin9), .pin10(_7408_1_pin10), .pin11(_7408_1_pin11), .pin12(s_t),
    .pin13(s_t), .pin14(1'b1));
  _7402 _7402_1 (
    .pin1(_7402_1_pin1), .pin2(_7402_1_pin2), .pin3(_7402_1_pin3), .pin4(_7402_1_pin4), .pin5(_7402_1_pin5),
    .pin6(_7402_1_pin6), .pin7(_7402_1_pin7), .pin8(1'b1), .pin9(1'b1), .pin10(1'b1), .pin12(1'b1),
    .pin13(1'b1), .pin14(1'b1));  // open: pin11
endmodule

/* Test case:
x y s out
0 0 0 0
0 1 0 0
1 0 0 0
0 0 1 0
1 1 0 1
0 1 1 1
1 0 1 1
1 1 1 1
*/
